// Logisim project Arch.circ as structural Verilog: 17 circuits, main circuit main
module main (
  input  [15:0] IN_PORT,
  input  Clk,
  input  Rst,
  input  Int,
  output [15:0] out_5
);

  wire cu_1_p4, cu_1_p5, cu_1_p7, cu_1_p8, cu_1_p9, cu_1_p10, cu_1_p12, cu_1_p13, cu_1_p14, cu_1_p15,
       cu_1_p16, cu_1_p17, dec_buff_1_is_alu_out;
  wire [1:0] cu_1_p6;
  wire [2:0] fetch_buff_1_write_addr_1, fetch_buff_1_write_addr_2;
  wire [3:0] cu_1_p11, dec_buff_1_alu_instr_out;
  wire [4:0] cu_1_p3;
  wire [15:0] dec_buff_1_op1, dec_buff_1_op2, dec_stage_1_dst, dec_stage_1_src, fetch_buff_1_data_1,
       fetch_buff_1_data_2, fetch_buff_1_full_instr, fetch_stage_1_instr, mem_stage_1_word, PC_q;
  wire [31:0] exec_stage_1_result;

  Register #(.width(16)) PC (.Q(PC_q));  // open: D, en, clk, clr
  Fetch_Stage fetch_stage_1 (.Clk(Clk), .PC(PC_q[8:0]), .Instr(fetch_stage_1_instr));
  Register #(.width(16)) OUT_PORT (.Q(out_5));  // open: D, en, clk, clr
  Register #(.width(16)) SP ();  // open: D, en, Q, clk, clr
  Fetch_Buff fetch_buff_1 (
    .Clk(Clk), .En(cu_1_p4), .Rst(cu_1_p5), .Instr(fetch_stage_1_instr), .Next_Addr(PC_q),
    .Full_Instr(fetch_buff_1_full_instr), .Data_1(fetch_buff_1_data_1), .Data_2(fetch_buff_1_data_2),
    .Write_Addr_1(fetch_buff_1_write_addr_1), .Write_Addr_2(fetch_buff_1_write_addr_2));
  // CU cu_1: pin names not known; wires that end beside it: Rst, Int, cu_1_p3, cu_1_p4, cu_1_p5, cu_1_p6, cu_1_p7, cu_1_p8, cu_1_p9, cu_1_p10, cu_1_p11, cu_1_p12, cu_1_p13, cu_1_p14, cu_1_p15, cu_1_p16, cu_1_p17
  Dec_Stage dec_stage_1 (
    .Clk(Clk), .Full_Instr(fetch_buff_1_full_instr), .Data_1(fetch_buff_1_data_1),
    .Data_2(fetch_buff_1_data_2), .Write_Addr_1(fetch_buff_1_write_addr_1),
    .Write_Addr_2(fetch_buff_1_write_addr_2), .LD_Imm(cu_1_p6), .Sel_Addr(cu_1_p7), .Opcode(cu_1_p3),
    .Src(dec_stage_1_src), .Dst(dec_stage_1_dst));
  Dec_Buff dec_buff_1 (
    .Clk(Clk), .En(cu_1_p8), .Rst(cu_1_p9), .Src(dec_stage_1_src), .Dst(dec_stage_1_dst),
    .Is_ALU_In(cu_1_p10), .ALU_Instr_In(cu_1_p11), .Is_ALU_Out(dec_buff_1_is_alu_out),
    .ALU_Instr_Out(dec_buff_1_alu_instr_out), .Op1(dec_buff_1_op1), .Op2(dec_buff_1_op2));
  Exec_Stage exec_stage_1 (
    .Clk(Clk), .Rst(cu_1_p12), .Is_ALU(dec_buff_1_is_alu_out), .ALU_Instr(dec_buff_1_alu_instr_out),
    .Op1(dec_buff_1_op1), .Op2(dec_buff_1_op2), .Result(exec_stage_1_result));
  Exec_Buff exec_buff_1 (
    .Clk(Clk), .Result(exec_stage_1_result), .En(cu_1_p13), .Rst(cu_1_p14), .Mem_W(cu_1_p15));  // open: R_W, Addr, Data
  Mem_Stage mem_stage_1 (.Clk(Clk), .Word(mem_stage_1_word));  // open: R_W, Addr, Data
  WB_Stage wb_stage_1 (.Clk(Clk));  // open: in_2, in_3
  Mem_Buff mem_buff_1 (.Clk(Clk), .Word(mem_stage_1_word), .En(cu_1_p16), .Rst(cu_1_p17));  // open: out_5, out_6
  // Pins of 9 and 16 bits meet at PC_q
endmodule

module Register_File (
  input  Clk,
  input  [15:0] Data_1,
  input  [15:0] Data_2,
  input  [2:0] Write_Addr_1,
  input  [2:0] Write_Addr_2,
  input  [2:0] Src_Addr,
  input  [2:0] Dst_Addr,
  output [15:0] Src,
  output [15:0] Dst
);

  wire decoder_1_out0, decoder_1_out1, decoder_1_out2, decoder_1_out3, decoder_1_out4, decoder_1_out5,
       decoder_2_out0, decoder_2_out1, decoder_2_out2, decoder_2_out3, decoder_2_out4, decoder_2_out5;
  wire [15:0] double_register_1_q, double_register_2_q, double_register_3_q, double_register_4_q,
       double_register_5_q, double_register_6_q;

  Decoder #(.select(3), .enable("false")) decoder_1 (
    .out0(decoder_1_out0), .out1(decoder_1_out1), .out2(decoder_1_out2), .out3(decoder_1_out3),
    .out4(decoder_1_out4), .out5(decoder_1_out5), .sel(Write_Addr_1));  // open: out6, out7
  Decoder #(.select(3), .enable("false")) decoder_2 (
    .out0(decoder_2_out0), .out1(decoder_2_out1), .out2(decoder_2_out2), .out3(decoder_2_out3),
    .out4(decoder_2_out4), .out5(decoder_2_out5), .sel(Write_Addr_2));  // open: out6, out7
  Double_Register double_register_1 (
    .D1(Data_1), .D2(Data_2), .En_1(decoder_1_out0), .En_2(decoder_2_out0), .Clk(Clk), .Q(double_register_1_q));
  Double_Register double_register_2 (
    .D1(Data_1), .D2(Data_2), .En_1(decoder_1_out3), .En_2(decoder_2_out3), .Clk(Clk), .Q(double_register_2_q));
  Multiplexer #(.select(3), .width(16), .enable("false")) multiplexer_1 (
    .in0(double_register_1_q), .in1(double_register_2_q), .in2(double_register_3_q),
    .in3(double_register_4_q), .in4(double_register_5_q), .in5(double_register_6_q), .out(Src), .sel(Src_Addr));  // open: in6, in7
  Double_Register double_register_3 (
    .D1(Data_1), .D2(Data_2), .En_1(decoder_1_out1), .En_2(decoder_2_out1), .Clk(Clk), .Q(double_register_3_q));
  Double_Register double_register_4 (
    .D1(Data_1), .D2(Data_2), .En_1(decoder_1_out4), .En_2(decoder_2_out4), .Clk(Clk), .Q(double_register_4_q));
  Multiplexer #(.select(3), .width(16), .enable("false")) multiplexer_2 (
    .in0(double_register_1_q), .in1(double_register_2_q), .in2(double_register_3_q),
    .in3(double_register_4_q), .in4(double_register_5_q), .in5(double_register_6_q), .out(Dst), .sel(Dst_Addr));  // open: in6, in7
  Double_Register double_register_5 (
    .D1(Data_1), .D2(Data_2), .En_1(decoder_1_out2), .En_2(decoder_2_out2), .Clk(Clk), .Q(double_register_5_q));
  Double_Register double_register_6 (
    .D1(Data_1), .D2(Data_2), .En_1(decoder_1_out5), .En_2(decoder_2_out5), .Clk(Clk), .Q(double_register_6_q));
endmodule

module Fetch_Stage (
  input  Clk,
  input  [8:0] PC,
  output [15:0] Instr
);

  Instr_RAM instr_ram_1 (.Clk(Clk), .Addr(PC), .Instr(Instr));
endmodule

module Dec_Stage (
  input  Clk,
  input  [15:0] Full_Instr,
  input  [15:0] Data_1,
  input  [15:0] Data_2,
  input  [2:0] Write_Addr_1,
  input  [2:0] Write_Addr_2,
  input  [1:0] LD_Imm,
  input  Sel_Addr,
  output [4:0] Opcode,
  output [15:0] Src,
  output [15:0] Dst
);

  Register_File register_file_1 (
    .Clk(Clk), .Data_1(Data_1), .Data_2(Data_2), .Write_Addr_1(Write_Addr_1), .Write_Addr_2(Write_Addr_2),
    .Src_Addr(Full_Instr[10:8]), .Dst_Addr(Full_Instr[7:5]), .Src(Src), .Dst(Dst));

  assign Opcode = Full_Instr[15:11];
endmodule

module Exec_Stage (
  input  Clk,
  input  Rst,
  input  Is_ALU,
  input  [3:0] ALU_Instr,
  input  [15:0] Op1,
  input  [15:0] Op2,
  output [31:0] Result
);

  wire not_1_out;
  wire [3:0] alu_1_flags, CCR_q;
  wire [15:0] alu_1_result;
  wire [31:0] bit_extender_1_out, multip_1_result;

  Register #(.width(4)) CCR (.D(alu_1_flags), .en(Is_ALU), .clk(Clk), .Q(CCR_q), .clr(Rst));
  ALU alu_1 (.ALU_Instr(ALU_Instr), .Op1(Op1), .Op2(Op2), .C_In(CCR_q[2]), .Result(alu_1_result), .Flags(alu_1_flags));
  assign bit_extender_1_out = {{16{alu_1_result[15]}}, alu_1_result};  // Bit_Extender bit_extender_1
  Multip multip_1 (.Op1(Op1), .Op2(Op2), .Result(multip_1_result));
  not not_1 (not_1_out, Is_ALU);
  Multiplexer #(.width(32), .enable("false")) multiplexer_1 (
    .in0(bit_extender_1_out), .in1(multip_1_result), .out(Result), .sel(not_1_out));
endmodule

module Mem_Stage (
  input  Clk,
  input  R_W,
  input  [8:0] Addr,
  input  [15:0] Data,
  output [15:0] Word
);

  Data_RAM data_ram_1 (.Clk(Clk), .R_W(R_W), .Addr(Addr), .Data_In(Data), .Data_Out(Word));
endmodule

module WB_Stage (
  input  Clk,
  input  in_2,
  input  in_3
);
endmodule

module Instr_RAM (
  input  Clk,
  input  [8:0] Addr,
  output [15:0] Instr
);
endmodule

module Double_Register (
  input  [15:0] D1,
  input  [15:0] D2,
  input  En_1,
  input  En_2,
  input  Clk,
  output [15:0] Q
);

  wire or_1_out;
  wire [15:0] multiplexer_1_out;

  Register #(.width(16)) register_1 (.D(multiplexer_1_out), .en(or_1_out), .clk(Clk), .Q(Q));  // open: clr
  Multiplexer #(.width(16), .enable("false")) multiplexer_1 (.in0(D1), .in1(D2), .out(multiplexer_1_out), .sel(En_2));
  or or_1 (or_1_out, En_1, En_2);
endmodule

module CU (
  input  Rst,
  input  INT,
  input  [4:0] Opcode,
  output En_Fetch,
  output Rst_Fetch,
  output [1:0] LD_Imm,
  output Sel_Addr,
  output En_Dec,
  output Rst_Dec,
  output Is_ALU,
  output [3:0] ALU_Instr,
  output Rst_Flag,
  output En_Exec,
  output Rst_Exec,
  output Mem_W,
  output En_Mem,
  output Rst_Mem
);
endmodule

module ALU (
  input  [3:0] ALU_Instr,
  input  [15:0] Op1,
  input  [15:0] Op2,
  input  C_In,
  output [15:0] Result,
  output [3:0] Flags
);
endmodule

module Multip (
  input  [15:0] Op1,
  input  [15:0] Op2,
  output [31:0] Result
);
endmodule

module Data_RAM (
  input  Clk,
  input  R_W,
  input  [8:0] Addr,
  input  [15:0] Data_In,
  output [15:0] Data_Out
);
endmodule

module Fetch_Buff (
  input  Clk,
  input  En,
  input  Rst,
  input  [15:0] Instr,
  input  [15:0] Next_Addr,
  output [15:0] Full_Instr,
  output [15:0] Data_1,
  output [15:0] Data_2,
  output [2:0] Write_Addr_1,
  output [2:0] Write_Addr_2
);
endmodule

module Dec_Buff (
  input  Clk,
  input  En,
  input  Rst,
  input  [15:0] Src,
  input  [15:0] Dst,
  input  Is_ALU_In,
  input  [3:0] ALU_Instr_In,
  output Is_ALU_Out,
  output [3:0] ALU_Instr_Out,
  output [15:0] Op1,
  output [15:0] Op2
);
endmodule

module Exec_Buff (
  input  Clk,
  input  [31:0] Result,
  input  En,
  input  Rst,
  input  Mem_W,
  output R_W,
  output [8:0] Addr,
  output [15:0] Data
);
endmodule

module Mem_Buff (
  input  Clk,
  input  [15:0] Word,
  input  En,
  input  Rst,
  output out_5,
  output out_6
);
endmodule
